# Fritzing sketch Untitled Sketch 2 (saved by Fritzing 1.0.5)

parts:
  M1 = DOIT Esp32 DevKit v1 (30 pins long, 11 pins width) [part_number=ESP32S-PIN30]
  Part1 = HX711 Weighing Sensor Module
  microSD1 = MicroSD Card Module
  LED1 = smd LED [color="Red (633nm)" package="0603 [SMD]"]
  R1 = Resistor [tolerance=±5% power=0.25W resistance=220 package=THT]
  A1 = 2957N11 pressure sensor
  R2 = Resistor [tolerance=±5% power=0.25W resistance=20000 package=THT]
  R3 = Resistor [tolerance=±5% power=0.25W resistance=10000 package=THT]
  ZS-042_RTC1 = ZS-042 RTC Module
  RE1 = KY-040 Rotary encoder [package=THT]
  LCD2004-I2C1 = LCD2004-I2C

nets:
  3V3: M1.3V3, RE1.Vcc
  GND: M1.GND, Part1.GND, microSD1.GND, R1.Pin_1, A1.Pin_1, R2.Pin_0, ZS-042_RTC1.GND, RE1.GND
  N1: M1.D4, LED1.cathode
  N2: M1.D5, microSD1.CS
  N3: M1.D18, microSD1.SCK
  N4: M1.D19, microSD1.MISO
  N5: M1.D21, ZS-042_RTC1.SDA, LCD2004-I2C1.SDA
  N6: M1.D22, ZS-042_RTC1.SCL, LCD2004-I2C1.SCL
  N7: M1.D23, microSD1.MOSI
  N8: M1.D34, R2.Pin_1, R3.Pin_1
  N9: M1.D26, Part1.DO/RX
  N10: M1.D27, Part1.CK/TX
  VCC: M1.VIN, Part1.VCC, microSD1.VCC, A1.Pin_2, ZS-042_RTC1.VCC
  N11: LED1.anode, R1.Pin_0
  N12: A1.Pin_3, R3.Pin_0

custom parts:
  DOIT Esp32 DevKit v1 (30 pins long, 11 pins width): The DOIT Esp32 DevKit v1 is one of the development board created by DOIT to evaluate the ESP-WROOM-32 module. It is based on the ESP32 microcontroller that boasts Wifi, Bluetooth, Ethernet and Low Power support all in a single chip. (vanepp) made breadboard work, adjusted pin numbering and labels and reduced size of schematic and cleaned up pcb. This chip is 30pins long (2 x15) and 11 pins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
  2957N11 pressure sensor: Monitor and control vacuum pumps, air compressors, and hydraulics. These transmitters convert both pressure and vacuum into an electrical signal that can be interpreted by receiving devices, such as remote displays, programmable logic controllers, and motor speed controls.
  KY-040 Rotary encoder: KY-040 Rotary Encoder with switch on breakout borad from AZ Delivery
  LCD2004-I2C: A standard character display with 4x20 characters. Comes in many colors with LCM2004 IIC attached.
